# Fritzing sketch ItsyBitsy_01_LED (saved by Fritzing 1.0.0rc)
breadboards: 1

parts:
  Part1 = adafruit [part_number="Adafruit #3800"]
  LED1 = LED - 5mm [color="Green (560nm)" current=0.030A package="5 mm [THT]"]
  R1 = Resistor [tolerance=±5% power=0.25W resistance=330 package=THT]

nets:
  GND: Part1.connector83, R1.Pin_0
  N1: Part1.connector96, LED1.anode
  N2: LED1.cathode, R1.Pin_1
