# Fritzing sketch ItsyBitsy_01_stoplight (saved by Fritzing 1.0.0rc)
breadboards: 1

parts:
  LED2 = LED - 5mm [color="Yellow (595nm)" current=0.030A package="5 mm [THT]"]
  LED3 = LED - 5mm [color="Red (635nm)" current=0.030A package="5 mm [THT]"]
  SW2 = Momentary Switch [package=ksa_sealed_tac_switch]
  LED1 = LED - 5mm [color="Green (560nm)" current=0.030A package="5 mm [THT]"]
  R1 = Resistor [tolerance=±5% power=0.25W resistance=330 package=THT]
  R2 = Resistor [tolerance=±5% power=0.25W resistance=330 package=THT]
  R3 = Resistor [tolerance=±5% power=0.25W resistance=330 package=THT]
  Part1 = Adafruit ItsyBitsy M4 [part_number="Adafruit #3800"]

nets:
  N1: LED2.cathode, R2.Pin_1
  N2: LED2.anode, Part1.A3
  N3: LED3.cathode, R3.Pin_1
  N4: LED3.anode, Part1.A4
  N5: SW2.1, SW2.2, Part1.MISO
  GND: SW2.3, R1.Pin_0, R2.Pin_0, R3.Pin_0, Part1.GND
  N6: LED1.cathode, R1.Pin_1
  N7: LED1.anode, Part1.D2

custom parts:
  Adafruit ItsyBitsy M4: What's smaller than a Feather but larger than a Trinket? It's an Adafruit ItsyBitsy M4 Express featuring the Microchip ATSAMD51! Small, powerful, with a ultra fast ATSAMD51 Cortex M4 processor running at 120 MHz - this microcontroller board is perfect when you want something very compact, with a ton of horsepower and a bunch of pins. This Itsy is like a bullet train, with it's 120MHz Cortex M4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
