# Fritzing sketch ItsyBitsy_03_potentiometer (saved by Fritzing 1.0.0rc)
breadboards: 1

parts:
  Part1 = Adafruit ItsyBitsy M4 [part_number="Adafruit #3800"]
  LED1 = LED - 5mm [color="Green (560nm)" current=0.030A package="5 mm [THT]"]
  R1 = Resistor [tolerance=±5% power=0.25W resistance=330 package=THT]
  R5 = TRIMPOT [maximum_resistance=10kΩ knob_status=50% power=0.5W package=3386u]
  LED3 = LED - 5mm [color="Infrared (880nm)" current=0.030A package="5 mm [THT]"]
  PHOTOTRANS = LTR-301 [package=ltr-301]
  R2 = Resistor [tolerance=±5% power=0.25W resistance=100 package=THT]
  R4 = Resistor [tolerance=±5% power=0.25W resistance=10k package=THT]

nets:
  GND: Part1.GND, R1.Pin_0, R5.CW, PHOTOTRANS.E, R2.Pin_0
  N1: Part1.D2, LED1.anode
  N2: Part1.A1, PHOTOTRANS.C, R4.Pin_0
  N3: Part1.VHI, R5.WIPER
  N4: Part1.+3V3, R5.CCW, LED3.anode, R4.Pin_1
  N5: LED1.cathode, R1.Pin_1
  N6: LED3.cathode, R2.Pin_1

custom parts:
  Adafruit ItsyBitsy M4: What's smaller than a Feather but larger than a Trinket? It's an Adafruit ItsyBitsy M4 Express featuring the Microchip ATSAMD51! Small, powerful, with a ultra fast ATSAMD51 Cortex M4 processor running at 120 MHz - this microcontroller board is perfect when you want something very compact, with a ton of horsepower and a bunch of pins. This Itsy is like a bullet train, with it's 120MHz Cortex M4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
