# Fritzing sketch ItsyBitsy_05_speaker (saved by Fritzing 1.0.0rc)
breadboards: 1

parts:
  Part1 = Adafruit ItsyBitsy M4 [part_number="Adafruit #3800"]
  SW2 = Momentary Switch [package=ksa_sealed_tac_switch]
  PIEZO = Piezo Speaker
  R1 = Resistor [tolerance=±5% power=0.25W resistance=330 package=THT]
  LED1 = LED - 5mm [color="Green (560nm)" current=0.030A package="5 mm [THT]"]

nets:
  GND: Part1.GND, SW2.3, PIEZO.pin1, R1.Pin_0
  N1: Part1.D5_5V, PIEZO.pin2
  N2: Part1.D2, LED1.anode
  N3: Part1.MISO, SW2.1, SW2.2
  N4: R1.Pin_1, LED1.cathode

custom parts:
  Adafruit ItsyBitsy M4: What's smaller than a Feather but larger than a Trinket? It's an Adafruit ItsyBitsy M4 Express featuring the Microchip ATSAMD51! Small, powerful, with a ultra fast ATSAMD51 Cortex M4 processor running at 120 MHz - this microcontroller board is perfect when you want something very compact, with a ton of horsepower and a bunch of pins. This Itsy is like a bullet train, with it's 120MHz Cortex M4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
