# Fritzing sketch ItsyBitsy_08_battery (saved by Fritzing 1.0.0rc)
breadboards: 1

parts:
  Part1 = Adafruit ItsyBitsy M4 [part_number="Adafruit #3800"]
  SW1 = Toggle Switch [package=THT]
  BATT1 = Battery
  BATT2 = Battery

nets:
  6V: Part1.VBAT, SW1.L1
  GND: Part1.GND, BATT2.-
  USB: Part1.VBUS
  3V3: Part1.+3V3
  N1: SW1.COM, BATT1.+
  N2: BATT1.-, BATT2.+

notes:
  You can put 3.5V to 6VDC into VBAT and the circuitry will switch between VBAT and VBUS (5V) dynamically for you.
  3V3 is the regulated output from the onboard regulator. You can draw 500mA whether powered by USB or battery.

custom parts:
  Adafruit ItsyBitsy M4: What's smaller than a Feather but larger than a Trinket? It's an Adafruit ItsyBitsy M4 Express featuring the Microchip ATSAMD51! Small, powerful, with a ultra fast ATSAMD51 Cortex M4 processor running at 120 MHz - this microcontroller board is perfect when you want something very compact, with a ton of horsepower and a bunch of pins. This Itsy is like a bullet train, with it's 120MHz Cortex M4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
