# Fritzing sketch ItsyBitsy_09_stepper (saved by Fritzing 1.0.0rc)
breadboards: 1

parts:
  Part1 = Adafruit ItsyBitsy M4 [part_number="Adafruit #3800"]
  SW2 = Momentary Switch [package=ksa_sealed_tac_switch]
  LED1 = LED - 5mm [color="Green (560nm)" current=0.030A package="5 mm [THT]"]
  R1 = Resistor [tolerance=±5% power=0.25W resistance=330 package=THT]
  SM1 = 28BYJ-48 Stepper Motor [part_number=28BYJ-48]
  Driver1 = 28BYJ-48 Driver Module [part_number=ULN2003 package=THT]

nets:
  GND: Part1.GND, SW2.3, R1.Pin_0, Driver1.GND
  N1: Part1.VBUS, Driver1.Vmotor
  N2: Part1.D13, Driver1.IN1
  N3: Part1.D12, Driver1.IN2
  N4: Part1.D11, Driver1.IN3
  N5: Part1.D10, Driver1.IN4
  N6: Part1.D2, LED1.anode
  N7: Part1.MISO, SW2.1, SW2.2
  N8: LED1.cathode, R1.Pin_1
  N9: SM1.blue-pin, Driver1.blue-pin
  N10: SM1.pink-pin, Driver1.pink-pin
  N11: SM1.yellow-pin, Driver1.yellow-pin
  N12: SM1.orange-pin, Driver1.orange-pin
  N13: SM1.red-pin, Driver1.red-pin

custom parts:
  Adafruit ItsyBitsy M4: What's smaller than a Feather but larger than a Trinket? It's an Adafruit ItsyBitsy M4 Express featuring the Microchip ATSAMD51! Small, powerful, with a ultra fast ATSAMD51 Cortex M4 processor running at 120 MHz - this microcontroller board is perfect when you want something very compact, with a ton of horsepower and a bunch of pins. This Itsy is like a bullet train, with it's 120MHz Cortex M4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
  28BYJ-48 Stepper Motor: Unipolar Stepper Motor 28BYJ-48 Top coil - pink & orange Bottom coil - blue & yellow Common rail - red Connector pins: blue - pink - yellow - orange - red
  28BYJ-48 Driver Module: ULN2003 Driver Module for the 28BYJ-48 Unipolar Stepper Motor LED A - Blue wire - Bottom coil left LED B - Pink wire - Top coil left LED C - Yellow wire - Bottom coil right LED D - Orange wire - Top coil right Common rail - red Connector pins: blue - pink - yellow - orange - red Control pins - IN1 to IN4 Power pins - GND & Vmotor (5-12V) On/Off jumper (if removed, power to motor is cut).
