# Fritzing sketch ItsyBitsy_10_final (saved by Fritzing 1.0.0rc)
breadboards: 1

parts:
  Driver1 = 28BYJ-48 Driver Module [part_number=ULN2003 package=THT]
  Part1 = Adafruit ItsyBitsy M4 [part_number="Adafruit #3800"]
  LED2 = LED - 5mm [color="Yellow (595nm)" current=0.030A package="5 mm [THT]"]
  LED3 = LED - 5mm [color="Red (635nm)" current=0.030A package="5 mm [THT]"]
  SW2 = Momentary Switch [package=ksa_sealed_tac_switch]
  SM1 = 28BYJ-48 Stepper Motor [part_number=28BYJ-48]
  PIEZO = Piezo Speaker
  PHOTOTRANS = LTR-301 [package=ltr-301]
  LED1 = LED - 5mm [color="Green (560nm)" current=0.030A package="5 mm [THT]"]
  R1 = Resistor [tolerance=±5% power=0.25W resistance=330 package=THT]
  R2 = Resistor [tolerance=±5% power=0.25W resistance=330 package=THT]
  R3 = Resistor [tolerance=±5% power=0.25W resistance=330 package=THT]
  R4 = Resistor [tolerance=±5% power=0.25W resistance=10k package=THT]
  SW1 = Toggle Switch [package=THT]
  BATT1 = Battery
  BATT2 = Battery
  Driver2 = 28BYJ-48 Driver Module [part_number=ULN2003 package=THT]
  SM2 = 28BYJ-48 Stepper Motor [part_number=28BYJ-48]
  J1 = Basic Servo

nets:
  N1: Driver1.IN1, Part1.D13
  N2: Driver1.IN2, Part1.D12
  N3: Driver1.IN3, Part1.D11
  N4: Driver1.IN4, Part1.D10
  GND: Driver1.GND, Part1.GND, SW2.3, PIEZO.pin1, PHOTOTRANS.E, R1.Pin_0, R2.Pin_0, R3.Pin_0, BATT2.-, Driver2.GND, J1.gnd
  6V: Driver1.Vmotor, Part1.VBAT, SW1.L1, Driver2.Vmotor, J1.vcc
  N5: Driver1.blue-pin, SM1.blue-pin
  N6: Driver1.pink-pin, SM1.pink-pin
  N7: Driver1.yellow-pin, SM1.yellow-pin
  N8: Driver1.orange-pin, SM1.orange-pin
  N9: Driver1.red-pin, SM1.red-pin
  USB: Part1.VBUS
  D7: Part1.D7, J1.pulse
  D5: Part1.D5_5V, PIEZO.pin2
  N10: Part1.SCL, Driver2.IN1
  N11: Part1.SDA, Driver2.IN2
  N12: Part1.TX_D1, Driver2.IN3
  N13: Part1.RX_D0, Driver2.IN4
  N14: Part1.D2, LED1.anode
  N15: Part1.MISO, SW2.1, SW2.2
  N16: Part1.A4, LED3.anode
  N17: Part1.A3, LED2.anode
  Ain: Part1.A1, PHOTOTRANS.C, R4.Pin_0
  3V3: Part1.+3V3, R4.Pin_1
  N18: LED2.cathode, R2.Pin_1
  N19: LED3.cathode, R3.Pin_1
  N20: LED1.cathode, R1.Pin_1
  N21: SW1.COM, BATT1.+
  N22: BATT1.-, BATT2.+
  N23: Driver2.blue-pin, SM2.blue-pin
  N24: Driver2.pink-pin, SM2.pink-pin
  N25: Driver2.yellow-pin, SM2.yellow-pin
  N26: Driver2.orange-pin, SM2.orange-pin
  N27: Driver2.red-pin, SM2.red-pin

notes:
  You can put 3.5V to 6VDC into VBAT and the circuitry will switch between VBAT and VBUS (5V) dynamically for you.
  D5 is a special OUTPUT-only pin that can PWM. It is level-shifted up to Vhi (VBAT or VBUS) voltage.
  3V3 is the regulated output from the onboard regulator. You can draw 500mA whether powered by USB or battery.

custom parts:
  28BYJ-48 Driver Module: ULN2003 Driver Module for the 28BYJ-48 Unipolar Stepper Motor LED A - Blue wire - Bottom coil left LED B - Pink wire - Top coil left LED C - Yellow wire - Bottom coil right LED D - Orange wire - Top coil right Common rail - red Connector pins: blue - pink - yellow - orange - red Control pins - IN1 to IN4 Power pins - GND & Vmotor (5-12V) On/Off jumper (if removed, power to motor is cut).
  Adafruit ItsyBitsy M4: What's smaller than a Feather but larger than a Trinket? It's an Adafruit ItsyBitsy M4 Express featuring the Microchip ATSAMD51! Small, powerful, with a ultra fast ATSAMD51 Cortex M4 processor running at 120 MHz - this microcontroller board is perfect when you want something very compact, with a ton of horsepower and a bunch of pins. This Itsy is like a bullet train, with it's 120MHz Cortex M4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
  28BYJ-48 Stepper Motor: Unipolar Stepper Motor 28BYJ-48 Top coil - pink & orange Bottom coil - blue & yellow Common rail - red Connector pins: blue - pink - yellow - orange - red
