# Fritzing sketch PicoRobot (saved by Fritzing 1.0.0rc)
breadboards: 1

parts:
  Mod1 = Raspberry Pi Pico
  SPST = Toggle Switch [package=THT]
  D2 = Rectifier Diode [part_number=1N4001 package="Melf DO-213 AB [SMD]"]
  SM1 = 28BYJ-48 Stepper Motor [part_number=28BYJ-48]
  Driver1 = 28BYJ-48 Driver Module [part_number=ULN2003 package=THT]
  VCC2 = Battery
  VCC3 = Battery
  LED1 = LED - 5mm [color="Green (565nm)" current=0.030A package="5 mm [THT]"]
  R1 = Resistor [tolerance=±5% power=0.25W resistance=1k package=THT]
  Driver2 = 28BYJ-48 Driver Module [part_number=ULN2003 package=THT]
  SM2 = 28BYJ-48 Stepper Motor [part_number=28BYJ-48]
  J1 = Basic Servo
  Q1 = QRD1114 [package=qrd1114]  # not connected

nets:
  GND: Mod1.pin_3, Mod1.pin_8, Mod1.pin_13, Mod1.pin_18, Mod1.pin_23, Mod1.pin_28, Mod1.pin_33, Mod1.pin_38, Driver1.GND, VCC3.-, R1.Pin_0, Driver2.GND, J1.gnd
  N1: Mod1.pin_4, Driver1.IN4
  N2: Mod1.pin_5, Driver1.IN3
  N3: Mod1.pin_6, Driver1.IN2
  N4: Mod1.pin_7, Driver1.IN1
  N5: Mod1.pin_14, Driver2.IN4
  N6: Mod1.pin_15, Driver2.IN3
  N7: Mod1.pin_16, Driver2.IN2
  N8: Mod1.pin_17, Driver2.IN1
  N9: Mod1.pin_21, LED1.anode
  N10: Mod1.pin_26, J1.pulse
  N11: Mod1.pin_39, D2.cathode
  6V: SPST.L1, D2.anode, Driver1.Vmotor, Driver2.Vmotor, J1.vcc
  N12: SPST.COM, VCC2.+
  N13: SM1.blue-pin, Driver1.blue-pin
  N14: SM1.pink-pin, Driver1.pink-pin
  N15: SM1.yellow-pin, Driver1.yellow-pin
  N16: SM1.orange-pin, Driver1.orange-pin
  N17: SM1.red-pin, Driver1.red-pin
  N18: VCC2.-, VCC3.+
  N19: LED1.cathode, R1.Pin_1
  N20: Driver2.blue-pin, SM2.blue-pin
  N21: Driver2.pink-pin, SM2.pink-pin
  N22: Driver2.yellow-pin, SM2.yellow-pin
  N23: Driver2.orange-pin, SM2.orange-pin
  N24: Driver2.red-pin, SM2.red-pin

custom parts:
  Raspberry Pi Pico: Raspberry Pi Pico. Based around the RP2040 microcontroller the Pico is a low cost microcontroller device bringing Raspberry Pi quality, cost, and easy of use to the microcontroller space. Jan 2021, Split part in to two versions: tht (this one) and SMD. This one will drill holes for a .1 in header in pcb to allow plugging in the module as well as providing pads to solder the module to the top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
  28BYJ-48 Stepper Motor: Unipolar Stepper Motor 28BYJ-48 Top coil - pink & orange Bottom coil - blue & yellow Common rail - red Connector pins: blue - pink - yellow - orange - red
  28BYJ-48 Driver Module: ULN2003 Driver Module for the 28BYJ-48 Unipolar Stepper Motor LED A - Blue wire - Bottom coil left LED B - Pink wire - Top coil left LED C - Yellow wire - Bottom coil right LED D - Orange wire - Top coil right Common rail - red Connector pins: blue - pink - yellow - orange - red Control pins - IN1 to IN4 Power pins - GND & Vmotor (5-12V) On/Off jumper (if removed, power to motor is cut).
